# Fritzing sketch Radar (saved by Fritzing 0.9.3b)
breadboards: 2

parts:
  J1 = Basic Servo
  hc-sr1 = hc-sr04
  Part1 = Arduino Uno (Rev3) - ICSP
  R1 = Resistor [tolerance=±5% resistance=220 package=THT]
  Raspberry_Pi3 = Raspberry Pi 3 [part_number=RPI-3-V1.2]
  CONN1 = USB connector [package=THT]
  CONN2 = USB connector [package=THT]
  LED1 = LED - 5mm [color="Red (633nm)" package="5 mm [THT]"]
  LED2 = LED - 5mm [color="Green (565nm)" package="5 mm [THT]"]
  LED3 = LED - 5mm [color="Green (565nm)" package="5 mm [THT]"]
  R2 = Resistor [tolerance=±5% resistance=220 package=THT]
  R3 = Resistor [tolerance=±5% resistance=220 package=THT]
  S1 = Pushbutton [package="[THT]"]
  S2 = Pushbutton [package="[THT]"]
  R7 = Resistor [tolerance=±5% resistance=10k package=THT]
  R8 = Resistor [tolerance=±5% resistance=10k package=THT]
  R10 = Resistor [tolerance=±5% resistance=220 package=THT]
  LED5 = LED - 5mm [color="Green (565nm)" package="5 mm [THT]"]

nets:
  GND: J1.gnd, hc-sr1.GND, Part1.GND, LED5.cathode
  VCC: J1.vcc, hc-sr1.VCC, Part1.5V
  N1: J1.pulse, Part1.D5_PWM
  N2: hc-sr1.Trig, Part1.D9_PWM
  N3: hc-sr1.Echo, Part1.D8
  N4: Part1.D2, R10.Pin_1
  N5: R1.Pin_0, LED3.anode
  N6: R1.Pin_1, Raspberry_Pi3.GPIO10
  N7: Raspberry_Pi3.GPIO9, R2.Pin_1
  N8: Raspberry_Pi3.GPIO11, R3.Pin_1
  N9: Raspberry_Pi3.GND, LED1.cathode, LED2.cathode, LED3.cathode, R7.Pin_0, R8.Pin_0
  N10: Raspberry_Pi3.GPIO24, S1.Pin_3, S1.Pin_4, R8.Pin_1
  N11: Raspberry_Pi3.GPIO23, S2.Pin_3, S2.Pin_4, R7.Pin_1
  N12: Raspberry_Pi3.5V, S1.Pin_1, S1.Pin_2, S2.Pin_1, S2.Pin_2
  5V: CONN1.5V, CONN2.5V
  N13: CONN1.d-, CONN2.d-
  N14: CONN1.d+, CONN2.d+
  GND_2: CONN1.GND, CONN1.chassis5, CONN1.chassis6, CONN2.GND, CONN2.chassis5, CONN2.chassis6
  N15: LED1.anode, R3.Pin_0
  N16: LED2.anode, R2.Pin_0
  N17: R10.Pin_0, LED5.anode
